# Fritzing sketch button_box_v2 (saved by Fritzing 0.9.4)
perfboards: 1

parts:
  WeMos_D1_Mini1 = WeMos D1 Mini
  S4_-_White = Pushbutton [package=THT]
  R1 = Resistor [tolerance=±1% resistance=470 package="2512 [SMD]"]
  R2 = Resistor [tolerance=±1% resistance=2k package="2512 [SMD]"]
  R3 = Resistor [tolerance=±1% resistance=5.1k package="2512 [SMD]"]
  S3_-_Yellow = Pushbutton [package=THT]
  S2_-_Green = Pushbutton [package=THT]
  S1_-_Red = Pushbutton [package=THT]
  S5_-_16mm_Silver = Pushbutton [package=THT]
  DS1 = DS18B20 1-Wire Temperature Sensor [part_number=DS18B20]
  R4 = Resistor [tolerance=±5% resistance=4.7k package=THT]
  LED1 = RGB LED (com. cathode, rbg) [package="5 mm [THT]"]

nets:
  3V3: WeMos_D1_Mini1.3V3, DS1.VDD, R4.Pin_1
  N1: WeMos_D1_Mini1.D0, R3.Pin_1
  N2: WeMos_D1_Mini1.D1, S1_-_Red.leg0
  N3: WeMos_D1_Mini1.D2, S2_-_Green.leg0
  N4: WeMos_D1_Mini1.D3, S3_-_Yellow.leg0
  N5: WeMos_D1_Mini1.D4, S4_-_White.leg0
  N6: WeMos_D1_Mini1.D5, R2.Pin_1
  N7: WeMos_D1_Mini1.D6, R1.Pin_1
  N8: WeMos_D1_Mini1.D7, S5_-_16mm_Silver.leg0
  N9: WeMos_D1_Mini1.D8, DS1.DQ, R4.Pin_0
  N10: WeMos_D1_Mini1.G, S4_-_White.leg1, S3_-_Yellow.leg1, S2_-_Green.leg1, S1_-_Red.leg1, S5_-_16mm_Silver.leg1, DS1.GND
  N11: R1.Pin_0, LED1.red_anode
  N12: R2.Pin_0, LED1.blue_anode
  N13: R3.Pin_0, LED1.green_anode
